# Fritzing sketch ShoutingGame (saved by Fritzing 0.9.3b)
breadboards: 1

parts:
  부품1 = Arduino Uno (Rev3)
  LED1 = LED - 5mm [color="Red (633nm)" package="5 mm [THT]"]
  LED2 = LED - 5mm [color="Red (633nm)" package="5 mm [THT]"]
  LED3 = LED - 5mm [color="Red (633nm)" package="5 mm [THT]"]
  LED4 = LED - 5mm [color="Red (633nm)" package="5 mm [THT]"]
  부품2 = Breakout Board for Electret Microphone

nets:
  N1: 부품1.A0, 부품2.AUD
  N2: 부품1.D10_PWM/SS, LED4.anode
  N3: 부품1.D11_PWM/MOSI, LED2.anode
  N4: 부품1.D12/MISO, LED3.anode
  N5: 부품1.D13/SCK, LED1.anode
  5V: 부품1.5V, 부품2.VCC
  GND: 부품1.GND, LED1.cathode, LED2.cathode, LED3.cathode, LED4.cathode, 부품2.GND
